# Fritzing sketch Basic Circuit Voltage Regulated (saved by Fritzing 0.9.3b)
perfboards: 1

parts:
  U1 = attiny85 [package=dip]
  U2 = Voltage Regulator - 5V [package="TO220 [THT]"]

nets:
  N1: U1.Pin_8, U2.output_voltage

notes:
  pin 0
  pin 1
  pin 2 (A1)
  pin 3 (A2)
  pin 4 (A3)
  +5V
  GND
  3V-35V
