# Fritzing sketch Audio Circuit Voltage Regulated (saved by Fritzing 0.9.3b)
perfboards: 1

parts:
  U1 = attiny85 [package=dip]
  Q1 = pnp-Powertransistor [package="TO220 [THT]"]
  U2 = Voltage Regulator - 5V [package="TO220 [THT]"]
  R2 = Resistor [tolerance=±5% resistance=1k package=THT]

nets:
  N1: U1.Pin_4, Q1.emitter, U2.GND
  N2: U1.Pin_5, R2.Pin_1
  N3: U1.Pin_8, U2.output_voltage
  N4: Q1.base, R2.Pin_0

notes:
  pin 0
  pin 1
  pin 2 (A1)
  pin 3 (A2)
  pin 4 (A3)
  +5V
  GND
  GND (Speaker)
  3V-35V
