# Fritzing sketch Audio Circuit (saved by Fritzing 0.9.3b)
perfboards: 1

parts:
  U1 = attiny85 [package=dip]
  Q1 = pnp-Powertransistor [package="TO220 [THT]"]
  R1 = Resistor [tolerance=±5% resistance=1.5k package=THT]

nets:
  N1: U1.Pin_4, Q1.emitter
  N2: U1.Pin_5, R1.Pin_1
  N3: Q1.base, R1.Pin_0

notes:
  pin 0
  pin 1
  pin 2 (A1)
  pin 3 (A2)
  pin 4 (A3)
  +5V
  GND
  GND (Speaker)
  +9V
