# Fritzing sketch Audio Circuit Step 1 (saved by Fritzing 0.9.3b)
perfboards: 1

parts:
  VCC2 = 4 x AAA Battery Mount
  U3 = attiny85 [package=dip]
  R3 = Resistor [tolerance=±5% resistance=1k package=THT]
  Q2 = pnp-Powertransistor [package="TO220 [THT]"]
  U4 = Voltage Regulator - 5V [package="TO220 [THT]"]

nets:
  N1: VCC2.-, U3.Pin_4, Q2.emitter, U4.GND
  N2: VCC2.+, U4.input_voltage
  N3: U3.Pin_5, R3.Pin_1
  N4: U3.Pin_8, U4.output_voltage
  N5: R3.Pin_0, Q2.base

notes:
  It is best to run the ground "rail" underneath the wires on the spider, and the power (+5V) rail on the outside
  Connect the power supply here (anywhere from 3V to 35V, or what your speaker can handle) - make sure not to let it connect to the +5V
  Run the power and ground rails around the spider for easy access
