# Fritzing sketch Audio Circuit Step 2 (saved by Fritzing 0.9.3b)
perfboards: 1

parts:
  SP1 = SPEAKER [package=pcb_mount_speaker]
  U5 = attiny85 [package=dip]
  VCC3 = 4 x AAA Battery Mount
  R4 = Resistor [tolerance=±5% resistance=1k package=THT]
  Q3 = pnp-Powertransistor [package="TO220 [THT]"]
  U6 = Voltage Regulator - 5V [package="TO220 [THT]"]

nets:
  N1: SP1.+, Q3.collector
  N2: SP1.-, VCC3.+, U6.input_voltage
  N3: U5.Pin_4, VCC3.-, Q3.emitter, U6.GND
  N4: U5.Pin_5, R4.Pin_1
  N5: U5.Pin_8, U6.output_voltage
  N6: R4.Pin_0, Q3.base

notes:
  Attach a speaker to the speaker power and GND (this can be a paper speaker or any type)
