# Fritzing sketch Audio Circuit Step 3 (saved by Fritzing 0.9.3b)
perfboards: 1

parts:
  R2 = Resistor [tolerance=±5% resistance=220 package=THT]  # not connected
  R3 = Resistor [tolerance=±5% resistance=220 package=THT]  # not connected
  SP2 = SPEAKER [package=pcb_mount_speaker]
  U7 = attiny85 [package=dip]
  VCC4 = 4 x AAA Battery Mount
  R5 = Resistor [tolerance=±5% resistance=1k package=THT]
  Q4 = pnp-Powertransistor [package="TO220 [THT]"]
  U8 = Voltage Regulator - 5V [package="TO220 [THT]"]

nets:
  N1: SP2.+, Q4.collector
  N2: SP2.-, VCC4.+, U8.input_voltage
  N3: U7.Pin_4, VCC4.-, Q4.emitter, U8.GND
  N4: U7.Pin_5, R5.Pin_1
  N5: U7.Pin_8, U8.output_voltage
  N6: R5.Pin_0, Q4.base

notes:
  Attach some kind of switch from pin 4 and pin 5 to the +5V strip - it can be any kind of button, toggle or switch
  You may want to use a pull-down resistor or a strip to +5V for on and one to GND for off
  (see LED Circuit step 3)
  RESISTORS OPTIONAL
  1
  2
