# Fritzing sketch Audio Circuit Step 4 (saved by Fritzing 0.9.3b)
perfboards: 1

parts:
  R4 = Rotary Potentiometer (Small) [maximum_resistance=100kΩ package=THT]  # not connected
  R5 = Resistor [tolerance=±5% resistance=1M package=THT]  # not connected
  U9 = attiny85 [package=dip]
  SP3 = SPEAKER [package=pcb_mount_speaker]
  R6 = Resistor [tolerance=±5% resistance=220 package=THT]  # not connected
  R7 = Resistor [tolerance=±5% resistance=220 package=THT]  # not connected
  R8 = Resistor [tolerance=±5% resistance=1k package=THT]
  Q5 = pnp-Powertransistor [package="TO220 [THT]"]
  U10 = Voltage Regulator - 5V [package="TO220 [THT]"]
  VCC5 = 4 x AAA Battery Mount

nets:
  N1: U9.Pin_4, Q5.emitter, U10.GND, VCC5.-
  N2: U9.Pin_5, R8.Pin_1
  N3: U9.Pin_8, U10.output_voltage
  N4: SP3.+, Q5.collector
  N5: SP3.-, U10.input_voltage, VCC5.+
  N6: R8.Pin_0, Q5.base

notes:
  Move this along to change resistance
  Attach some kind of device with variable resistance by attaching it to +5V and ground (run a current through it) and then attach the spider's voltage-reading pin somewhere in the middle for it to measure the resistance
  For most potentiometers, the outside pins are the power and ground, and the middle pin is the voltage signal
  You can also create your own resistor by moving a contact along pencil lead or even your skin (you'll need a 1M Ohm resistor) - see LED Circuit step 4
  2
  1
