# Fritzing sketch Basic Circuit Step 1 (saved by Fritzing 0.9.3b)
perfboards: 1

parts:
  VCC1 = 4 x AAA Battery Mount  # not connected
  U3 = attiny85 [package=dip]
  U4 = Voltage Regulator - 5V [package="TO220 [THT]"]

nets:
  N1: U3.Pin_8, U4.output_voltage

notes:
  It is best to run the ground "rail" underneath the wires on the spider, and the power (+5V) rail on the outside
  Connect the power supply here (anywhere from 3V to 35V) - make sure not to let it connect to the +5V
  Run the power and ground rails around the spider for easy access
