# Fritzing sketch Basic Circuit Step 2 (saved by Fritzing 0.9.3b)
perfboards: 1

parts:
  LED3 = LED - 5mm [color="Red (633nm)" package="5 mm [THT]"]
  LED2 = LED - 5mm [color="Red (633nm)" package="5 mm [THT]"]
  U4 = Voltage Regulator - 5V [package="TO220 [THT]"]
  VCC2 = 4 x AAA Battery Mount
  U3 = attiny85 [package=dip]
  LED1 = LED - 5mm [color="Red (633nm)" package="5 mm [THT]"]

nets:
  N1: LED3.anode, U3.Pin_5
  N2: LED2.anode, U3.Pin_6
  N3: U4.output_voltage, U3.Pin_8
  N4: VCC2.-, U3.Pin_4
  N5: U3.Pin_7, LED1.anode

notes:
  Wire up 3 LEDs to pins 0, 1, and 2 (on the right side), connecting the positive side to the pin and the negative to ground
  (The negative side has a flat face and a shorter leg)
