# Fritzing sketch Basic Circuit Step 3 (saved by Fritzing 0.9.3b)
perfboards: 1

parts:
  S1 = Pushbutton [package="[THT]"]  # not connected
  S2 = Toggle Switch [package=THT]  # not connected
  R1 = Resistor [tolerance=±5% resistance=220 package=THT]  # not connected
  LED4 = LED - 5mm [color="Red (633nm)" package="5 mm [THT]"]
  LED5 = LED - 5mm [color="Red (633nm)" package="5 mm [THT]"]
  LED6 = LED - 5mm [color="Red (633nm)" package="5 mm [THT]"]
  U5 = attiny85 [package=dip]
  VCC3 = 4 x AAA Battery Mount
  U6 = Voltage Regulator - 5V [package="TO220 [THT]"]

nets:
  N1: LED4.anode, U5.Pin_7
  N2: LED5.anode, U5.Pin_6
  N3: LED6.anode, U5.Pin_5
  N4: U5.Pin_4, VCC3.-
  N5: U5.Pin_8, U6.output_voltage

notes:
  OR
  Attach some kind of switch from pin 4 to the +5V strip - it can be any kind of button, toggle or switch
  (The input you get may be less sporadic if you add a "pull-down resistor" going from the pin to ground)
  OPTIONAL
  Alternatively (to avoid resistors) you can add two strips, one going to GND and the other to +5V, and touch one for on and one for off.
