# Fritzing sketch Basic Circuit Step 4 pt 1 (saved by Fritzing 0.9.3b)
perfboards: 1

parts:
  R1 = Resistor [tolerance=±5% resistance=220 package=THT]  # not connected
  R2 = Rotary Potentiometer (Small) [maximum_resistance=100kΩ package=THT]
  LED7 = LED - 5mm [color="Red (633nm)" package="5 mm [THT]"]
  LED8 = LED - 5mm [color="Red (633nm)" package="5 mm [THT]"]
  LED9 = LED - 5mm [color="Red (633nm)" package="5 mm [THT]"]
  U7 = attiny85 [package=dip]
  VCC4 = 4 x AAA Battery Mount
  U8 = Voltage Regulator - 5V [package="TO220 [THT]"]

nets:
  N1: R2.wiper, U7.Pin_3
  N2: LED7.anode, U7.Pin_7
  N3: LED8.anode, U7.Pin_6
  N4: LED9.anode, U7.Pin_5
  N5: U7.Pin_4, VCC4.-
  N6: U7.Pin_8, U8.output_voltage

notes:
  Attach some kind of device with variable resistance by attaching it to +5V and ground (run a current through it) and then attach the spider's voltage-reading pin somewhere in the middle for it to measure the resistance
  For most potentiometers, the outside pins are the power and ground, and the middle pin is the voltage signal
