# Fritzing sketch Basic Circuit Step 4 pt 2 (saved by Fritzing 0.9.3b)

parts:
  R3 = Resistor [tolerance=±5% resistance=1M package=THT]  # not connected
  R5 = Resistor [tolerance=±5% resistance=1M package=THT]
  R6 = Photocell (LDR) [package=THT]

nets:
  N1: R5.Pin_0, R6.pin_1

notes:
  You can also create your own resistor by moving a contact along pencil lead or even your skin (you'll need a 1M Ohm resistor)
  Move this along to change resistance
  This setup allows us to measure the current using a voltage divider; the microcontroller measures the voltage between the known resistor and ground, which depends on the resistance of the sensor
  known resistance
  variable resistance
  = variable current
  + variable current
  = variable voltage
  to input pin
