# Fritzing sketch Basic Circuit Step 4 (saved by Fritzing 0.9.3b)
perfboards: 1

parts:
  U1 = attiny85 [package=dip]
  VCC1 = 4 x AAA Battery Mount  # not connected
  LED1 = LED - 5mm [color="Red (633nm)" package="5 mm [THT]"]
  LED2 = LED - 5mm [color="Red (633nm)" package="5 mm [THT]"]
  LED3 = LED - 5mm [color="Red (633nm)" package="5 mm [THT]"]
  R1 = Resistor [tolerance=±5% resistance=220 package=THT]  # not connected
  R2 = Rotary Potentiometer (Small) [maximum_resistance=100kΩ package=THT]  # not connected
  R3 = Resistor [tolerance=±5% resistance=1M package=THT]  # not connected
  R5 = Resistor [tolerance=±5% resistance=1M package=THT]
  R6 = Photocell (LDR) [package=THT]

nets:
  N1: U1.Pin_5, LED3.anode
  N2: U1.Pin_6, LED2.anode
  N3: U1.Pin_7, LED1.anode
  N4: R5.Pin_0, R6.pin_1

notes:
  Attach some kind of device with variable resistance by attaching it to +5V and ground (run a current through it) and then attach the spider's voltage-reading pin to the right place for it to measure the resistance
  OR
  For most potentiometers, the outside pins are the power and ground, and the middle pin is the voltage signal
  You can also create your own resistor by moving a contact along pencil lead or even your skin (you'll need a 1M Ohm resistor)
  Move this along to change resistance
  This setup allows us to measure the current using a voltage divider; the microcontroller measures the voltage between the known resistor and ground, which depends on the resistance of the sensor
  known resistance
  variable resistance
  = variable current
  + variable current
  = variable voltage
