# Fritzing sketch Audio Circuit Step 3 (saved by Fritzing 0.9.3b)
perfboards: 1

parts:
  U1 = attiny85 [package=dip]
  Q1 = pnp-Powertransistor [package="TO220 [THT]"]
  R1 = Resistor [tolerance=±5% resistance=1k package=THT]
  VCC2 = 4 x AAA Battery Mount  # not connected
  VCC3 = Battery block 9V
  SP1 = SPEAKER [package=pcb_mount_speaker]
  R2 = Resistor [tolerance=±5% resistance=220 package=THT]  # not connected
  R3 = Resistor [tolerance=±5% resistance=220 package=THT]  # not connected

nets:
  N1: U1.Pin_4, Q1.emitter, VCC3.-
  N2: U1.Pin_5, R1.Pin_1
  N3: Q1.collector, SP1.+

notes:
  Attach some kind of switch from pin 4 and pin 5 to the +5V strip - it can be any kind of button, toggle or switch
  You may want to use a pull-down resistor or a strip to +5V for on and one to GND for off
  (see LED Circuit step 3)
  RESISTORS OPTIONAL
  1
  2
