# Fritzing sketch Audio Circuit Step 4 (saved by Fritzing 0.9.3b)
perfboards: 1

parts:
  U1 = attiny85 [package=dip]
  Q1 = pnp-Powertransistor [package="TO220 [THT]"]
  R1 = Resistor [tolerance=±5% resistance=1k package=THT]
  VCC2 = 4 x AAA Battery Mount  # not connected
  VCC3 = Battery block 9V
  SP1 = SPEAKER [package=pcb_mount_speaker]
  R2 = Resistor [tolerance=±5% resistance=220 package=THT]  # not connected
  R3 = Resistor [tolerance=±5% resistance=220 package=THT]  # not connected
  R4 = Rotary Potentiometer (Small) [maximum_resistance=100kΩ package=THT]  # not connected
  R5 = Resistor [tolerance=±5% resistance=1M package=THT]  # not connected

nets:
  N1: U1.Pin_4, Q1.emitter, VCC3.-
  N2: U1.Pin_5, R1.Pin_1
  N3: Q1.collector, SP1.+

notes:
  1
  2
  Move this along to change resistance
  Attach some kind of device with variable resistance by attaching it to +5V and ground (run a current through it) and then attach the spider's voltage-reading pin to the right place for it to measure the resistance
  For most potentiometers, the outside pins are the power and ground, and the middle pin is the voltage signal
  You can also create your own resistor by moving a contact along pencil lead or even your skin (you'll need a 1M Ohm resistor)
