# Fritzing sketch Basic Circuit Step 2 (saved by Fritzing 0.9.3b)
perfboards: 1

parts:
  U1 = attiny85 [package=dip]
  VCC1 = 4 x AAA Battery Mount  # not connected
  LED1 = LED - 5mm [color="Red (633nm)" package="5 mm [THT]"]
  LED2 = LED - 5mm [color="Red (633nm)" package="5 mm [THT]"]
  LED3 = LED - 5mm [color="Red (633nm)" package="5 mm [THT]"]

nets:
  N1: U1.Pin_5, LED3.anode
  N2: U1.Pin_6, LED2.anode
  N3: U1.Pin_7, LED1.anode

notes:
  Wire up 3 LEDs to pins 0, 1, and 2 (on the right side), connecting the positive side to the pin and the negative to ground
  (The negative side has a flat face and a shorter leg)
